// Logisim project cpu_16bit.circ as structural Verilog: 8 circuits, main circuit main
module full_adder (
  input  A,
  input  B,
  input  Cin,
  output Cout,
  output S
);

  wire and_1_out, and_2_out, and_3_out;

  and and_1 (and_1_out, A, B);
  and and_2 (and_2_out, A, Cin);
  and and_3 (and_3_out, B, Cin);
  or or_1 (Cout, and_1_out, and_2_out, and_3_out);
  xor xor_1 (S, A, B, Cin);

  // Notes on the sheet:
  //   AB
  //   ACin
  //   BCin
endmodule

module sixteen_bit_adder (
  input  [15:0] A,
  input  [15:0] B,
  input  Cin,
  output Cout,
  output [15:0] S
);

  wire full_adder_2_cout, full_adder_3_cout, full_adder_4_cout, full_adder_5_cout, full_adder_6_cout,
       full_adder_7_cout, full_adder_8_cout, full_adder_9_cout, full_adder_10_cout, full_adder_11_cout,
       full_adder_12_cout, full_adder_13_cout, full_adder_14_cout, full_adder_15_cout, full_adder_16_cout;

  full_adder full_adder_1 (.A(A[15]), .B(B[15]), .Cin(full_adder_2_cout), .Cout(Cout), .S(S[15]));
  full_adder full_adder_2 (.A(A[14]), .B(B[14]), .Cin(full_adder_3_cout), .Cout(full_adder_2_cout), .S(S[14]));
  full_adder full_adder_3 (.A(A[13]), .B(B[13]), .Cin(full_adder_4_cout), .Cout(full_adder_3_cout), .S(S[13]));
  full_adder full_adder_4 (.A(A[12]), .B(B[12]), .Cin(full_adder_5_cout), .Cout(full_adder_4_cout), .S(S[12]));
  full_adder full_adder_5 (.A(A[11]), .B(B[11]), .Cin(full_adder_6_cout), .Cout(full_adder_5_cout), .S(S[11]));
  full_adder full_adder_6 (.A(A[10]), .B(B[10]), .Cin(full_adder_7_cout), .Cout(full_adder_6_cout), .S(S[10]));
  full_adder full_adder_7 (.A(A[9]), .B(B[9]), .Cin(full_adder_8_cout), .Cout(full_adder_7_cout), .S(S[9]));
  full_adder full_adder_8 (.A(A[8]), .B(B[8]), .Cin(full_adder_9_cout), .Cout(full_adder_8_cout), .S(S[8]));
  full_adder full_adder_9 (.A(A[7]), .B(B[7]), .Cin(full_adder_10_cout), .Cout(full_adder_9_cout), .S(S[7]));
  full_adder full_adder_10 (.A(A[6]), .B(B[6]), .Cin(full_adder_11_cout), .Cout(full_adder_10_cout), .S(S[6]));
  full_adder full_adder_11 (.A(A[5]), .B(B[5]), .Cin(full_adder_12_cout), .Cout(full_adder_11_cout), .S(S[5]));
  full_adder full_adder_12 (.A(A[4]), .B(B[4]), .Cin(full_adder_13_cout), .Cout(full_adder_12_cout), .S(S[4]));
  full_adder full_adder_13 (.A(A[3]), .B(B[3]), .Cin(full_adder_14_cout), .Cout(full_adder_13_cout), .S(S[3]));
  full_adder full_adder_14 (.A(A[2]), .B(B[2]), .Cin(full_adder_15_cout), .Cout(full_adder_14_cout), .S(S[2]));
  full_adder full_adder_15 (.A(A[1]), .B(B[1]), .Cin(full_adder_16_cout), .Cout(full_adder_15_cout), .S(S[1]));
  full_adder full_adder_16 (.A(A[0]), .B(B[0]), .Cin(Cin), .Cout(full_adder_16_cout), .S(S[0]));
endmodule

module sixteen_bit_adder_and_subber (
  input  [15:0] A,
  input  [15:0] B,
  input  Op,
  output Cout,
  output [15:0] Sum
);

  wire [15:0] xor_1_out;

  assign xor_1_out = B ^ {16{Op}};  // XOR_Gate xor_1, 16 bits wide
  sixteen_bit_adder sixteen_bit_adder_1 (.A(A), .B(xor_1_out), .Cin(Op), .Cout(Cout), .S(Sum));
endmodule

module sixteen_bit_multiplier (
  input  [15:0] A,
  input  [15:0] B,
  output [31:0] Product
);

  wire [14:0] and_255_out;
  wire [15:0] and_211_out, and_212_out, and_213_out, and_214_out, and_215_out, and_216_out, and_217_out,
       and_218_out, and_219_out, and_220_out, and_221_out, and_222_out, and_223_out, and_224_out,
       and_240_out, sixteen_bit_adder_1_s, sixteen_bit_adder_2_s, sixteen_bit_adder_3_s,
       sixteen_bit_adder_4_s, sixteen_bit_adder_5_s, sixteen_bit_adder_6_s, sixteen_bit_adder_7_s,
       sixteen_bit_adder_8_s, sixteen_bit_adder_9_s, sixteen_bit_adder_10_s, sixteen_bit_adder_11_s,
       sixteen_bit_adder_12_s, sixteen_bit_adder_13_s, sixteen_bit_adder_14_s;

  and and_1 (and_211_out[15], A[15], B[2]);
  and and_2 (and_212_out[15], A[15], B[3]);
  and and_3 (and_213_out[15], A[15], B[4]);
  and and_4 (and_214_out[15], A[15], B[5]);
  and and_5 (and_215_out[15], A[15], B[6]);
  and and_6 (and_216_out[15], A[15], B[7]);
  and and_7 (and_217_out[15], A[15], B[8]);
  and and_8 (and_218_out[15], A[15], B[9]);
  and and_9 (and_219_out[15], A[15], B[10]);
  and and_10 (and_220_out[15], A[15], B[11]);
  and and_11 (and_221_out[15], A[15], B[12]);
  and and_12 (and_222_out[15], A[15], B[13]);
  and and_13 (and_223_out[15], A[15], B[14]);
  and and_14 (and_224_out[15], A[15], B[15]);
  and and_15 (and_211_out[14], A[14], B[2]);
  and and_16 (and_211_out[13], A[13], B[2]);
  and and_17 (and_212_out[14], A[14], B[3]);
  and and_18 (and_212_out[13], A[13], B[3]);
  and and_19 (and_213_out[14], A[14], B[4]);
  and and_20 (and_213_out[13], A[13], B[4]);
  and and_21 (and_214_out[14], A[14], B[5]);
  and and_22 (and_214_out[13], A[13], B[5]);
  and and_23 (and_215_out[14], A[14], B[6]);
  and and_24 (and_215_out[13], A[13], B[6]);
  and and_25 (and_216_out[14], A[14], B[7]);
  and and_26 (and_216_out[13], A[13], B[7]);
  and and_27 (and_217_out[14], A[14], B[8]);
  and and_28 (and_217_out[13], A[13], B[8]);
  and and_29 (and_218_out[14], A[14], B[9]);
  and and_30 (and_218_out[13], A[13], B[9]);
  and and_31 (and_219_out[14], A[14], B[10]);
  and and_32 (and_219_out[13], A[13], B[10]);
  and and_33 (and_220_out[14], A[14], B[11]);
  and and_34 (and_220_out[13], A[13], B[11]);
  and and_35 (and_221_out[14], A[14], B[12]);
  and and_36 (and_221_out[13], A[13], B[12]);
  and and_37 (and_222_out[14], A[14], B[13]);
  and and_38 (and_222_out[13], A[13], B[13]);
  and and_39 (and_223_out[14], A[14], B[14]);
  and and_40 (and_223_out[13], A[13], B[14]);
  and and_41 (and_224_out[14], A[14], B[15]);
  and and_42 (and_224_out[13], A[13], B[15]);
  and and_43 (and_211_out[12], A[12], B[2]);
  and and_44 (and_211_out[11], A[11], B[2]);
  and and_45 (and_212_out[12], A[12], B[3]);
  and and_46 (and_212_out[11], A[11], B[3]);
  and and_47 (and_213_out[12], A[12], B[4]);
  and and_48 (and_213_out[11], A[11], B[4]);
  and and_49 (and_214_out[12], A[12], B[5]);
  and and_50 (and_214_out[11], A[11], B[5]);
  and and_51 (and_215_out[12], A[12], B[6]);
  and and_52 (and_215_out[11], A[11], B[6]);
  and and_53 (and_216_out[12], A[12], B[7]);
  and and_54 (and_216_out[11], A[11], B[7]);
  and and_55 (and_217_out[12], A[12], B[8]);
  and and_56 (and_217_out[11], A[11], B[8]);
  and and_57 (and_218_out[12], A[12], B[9]);
  and and_58 (and_218_out[11], A[11], B[9]);
  and and_59 (and_219_out[12], A[12], B[10]);
  and and_60 (and_219_out[11], A[11], B[10]);
  and and_61 (and_220_out[12], A[12], B[11]);
  and and_62 (and_220_out[11], A[11], B[11]);
  and and_63 (and_221_out[12], A[12], B[12]);
  and and_64 (and_221_out[11], A[11], B[12]);
  and and_65 (and_222_out[12], A[12], B[13]);
  and and_66 (and_222_out[11], A[11], B[13]);
  and and_67 (and_223_out[12], A[12], B[14]);
  and and_68 (and_223_out[11], A[11], B[14]);
  and and_69 (and_224_out[12], A[12], B[15]);
  and and_70 (and_224_out[11], A[11], B[15]);
  and and_71 (and_211_out[10], A[10], B[2]);
  and and_72 (and_211_out[9], A[9], B[2]);
  and and_73 (and_212_out[10], A[10], B[3]);
  and and_74 (and_212_out[9], A[9], B[3]);
  and and_75 (and_213_out[10], A[10], B[4]);
  and and_76 (and_213_out[9], A[9], B[4]);
  and and_77 (and_214_out[10], A[10], B[5]);
  and and_78 (and_214_out[9], A[9], B[5]);
  and and_79 (and_215_out[10], A[10], B[6]);
  and and_80 (and_215_out[9], A[9], B[6]);
  and and_81 (and_216_out[10], A[10], B[7]);
  and and_82 (and_216_out[9], A[9], B[7]);
  and and_83 (and_217_out[10], A[10], B[8]);
  and and_84 (and_217_out[9], A[9], B[8]);
  and and_85 (and_218_out[10], A[10], B[9]);
  and and_86 (and_218_out[9], A[9], B[9]);
  and and_87 (and_219_out[10], A[10], B[10]);
  and and_88 (and_219_out[9], A[9], B[10]);
  and and_89 (and_220_out[10], A[10], B[11]);
  and and_90 (and_220_out[9], A[9], B[11]);
  and and_91 (and_221_out[10], A[10], B[12]);
  and and_92 (and_221_out[9], A[9], B[12]);
  and and_93 (and_222_out[10], A[10], B[13]);
  and and_94 (and_222_out[9], A[9], B[13]);
  and and_95 (and_223_out[10], A[10], B[14]);
  and and_96 (and_223_out[9], A[9], B[14]);
  and and_97 (and_224_out[10], A[10], B[15]);
  and and_98 (and_224_out[9], A[9], B[15]);
  and and_99 (and_211_out[7], A[7], B[2]);
  and and_100 (and_211_out[8], A[8], B[2]);
  and and_101 (and_212_out[7], A[7], B[3]);
  and and_102 (and_212_out[8], A[8], B[3]);
  and and_103 (and_213_out[7], A[7], B[4]);
  and and_104 (and_213_out[8], A[8], B[4]);
  and and_105 (and_214_out[7], A[7], B[5]);
  and and_106 (and_214_out[8], A[8], B[5]);
  and and_107 (and_215_out[7], A[7], B[6]);
  and and_108 (and_215_out[8], A[8], B[6]);
  and and_109 (and_216_out[7], A[7], B[7]);
  and and_110 (and_216_out[8], A[8], B[7]);
  and and_111 (and_217_out[7], A[7], B[8]);
  and and_112 (and_217_out[8], A[8], B[8]);
  and and_113 (and_218_out[7], A[7], B[9]);
  and and_114 (and_218_out[8], A[8], B[9]);
  and and_115 (and_219_out[7], A[7], B[10]);
  and and_116 (and_219_out[8], A[8], B[10]);
  and and_117 (and_220_out[7], A[7], B[11]);
  and and_118 (and_220_out[8], A[8], B[11]);
  and and_119 (and_221_out[7], A[7], B[12]);
  and and_120 (and_221_out[8], A[8], B[12]);
  and and_121 (and_222_out[7], A[7], B[13]);
  and and_122 (and_222_out[8], A[8], B[13]);
  and and_123 (and_223_out[7], A[7], B[14]);
  and and_124 (and_223_out[8], A[8], B[14]);
  and and_125 (and_224_out[7], A[7], B[15]);
  and and_126 (and_224_out[8], A[8], B[15]);
  and and_127 (and_211_out[6], A[6], B[2]);
  and and_128 (and_211_out[5], A[5], B[2]);
  and and_129 (and_212_out[6], A[6], B[3]);
  and and_130 (and_212_out[5], A[5], B[3]);
  and and_131 (and_213_out[6], A[6], B[4]);
  and and_132 (and_213_out[5], A[5], B[4]);
  and and_133 (and_214_out[6], A[6], B[5]);
  and and_134 (and_214_out[5], A[5], B[5]);
  and and_135 (and_215_out[6], A[6], B[6]);
  and and_136 (and_215_out[5], A[5], B[6]);
  and and_137 (and_216_out[6], A[6], B[7]);
  and and_138 (and_216_out[5], A[5], B[7]);
  and and_139 (and_217_out[6], A[6], B[8]);
  and and_140 (and_217_out[5], A[5], B[8]);
  and and_141 (and_218_out[6], A[6], B[9]);
  and and_142 (and_218_out[5], A[5], B[9]);
  and and_143 (and_219_out[6], A[6], B[10]);
  and and_144 (and_219_out[5], A[5], B[10]);
  and and_145 (and_220_out[6], A[6], B[11]);
  and and_146 (and_220_out[5], A[5], B[11]);
  and and_147 (and_221_out[6], A[6], B[12]);
  and and_148 (and_221_out[5], A[5], B[12]);
  and and_149 (and_222_out[6], A[6], B[13]);
  and and_150 (and_222_out[5], A[5], B[13]);
  and and_151 (and_223_out[6], A[6], B[14]);
  and and_152 (and_223_out[5], A[5], B[14]);
  and and_153 (and_224_out[6], A[6], B[15]);
  and and_154 (and_224_out[5], A[5], B[15]);
  and and_155 (and_211_out[4], A[4], B[2]);
  and and_156 (and_211_out[3], A[3], B[2]);
  and and_157 (and_212_out[4], A[4], B[3]);
  and and_158 (and_212_out[3], A[3], B[3]);
  and and_159 (and_213_out[4], A[4], B[4]);
  and and_160 (and_213_out[3], A[3], B[4]);
  and and_161 (and_214_out[4], A[4], B[5]);
  and and_162 (and_214_out[3], A[3], B[5]);
  and and_163 (and_215_out[4], A[4], B[6]);
  and and_164 (and_215_out[3], A[3], B[6]);
  and and_165 (and_216_out[4], A[4], B[7]);
  and and_166 (and_216_out[3], A[3], B[7]);
  and and_167 (and_217_out[4], A[4], B[8]);
  and and_168 (and_217_out[3], A[3], B[8]);
  and and_169 (and_218_out[4], A[4], B[9]);
  and and_170 (and_218_out[3], A[3], B[9]);
  and and_171 (and_219_out[4], A[4], B[10]);
  and and_172 (and_219_out[3], A[3], B[10]);
  and and_173 (and_220_out[4], A[4], B[11]);
  and and_174 (and_220_out[3], A[3], B[11]);
  and and_175 (and_221_out[4], A[4], B[12]);
  and and_176 (and_221_out[3], A[3], B[12]);
  and and_177 (and_222_out[4], A[4], B[13]);
  and and_178 (and_222_out[3], A[3], B[13]);
  and and_179 (and_223_out[4], A[4], B[14]);
  and and_180 (and_223_out[3], A[3], B[14]);
  and and_181 (and_224_out[4], A[4], B[15]);
  and and_182 (and_224_out[3], A[3], B[15]);
  and and_183 (and_211_out[2], A[2], B[2]);
  and and_184 (and_211_out[1], A[1], B[2]);
  and and_185 (and_212_out[2], A[2], B[3]);
  and and_186 (and_212_out[1], A[1], B[3]);
  and and_187 (and_213_out[2], A[2], B[4]);
  and and_188 (and_213_out[1], A[1], B[4]);
  and and_189 (and_214_out[2], A[2], B[5]);
  and and_190 (and_214_out[1], A[1], B[5]);
  and and_191 (and_215_out[2], A[2], B[6]);
  and and_192 (and_215_out[1], A[1], B[6]);
  and and_193 (and_216_out[2], A[2], B[7]);
  and and_194 (and_216_out[1], A[1], B[7]);
  and and_195 (and_217_out[2], A[2], B[8]);
  and and_196 (and_217_out[1], A[1], B[8]);
  and and_197 (and_218_out[2], A[2], B[9]);
  and and_198 (and_218_out[1], A[1], B[9]);
  and and_199 (and_219_out[2], A[2], B[10]);
  and and_200 (and_219_out[1], A[1], B[10]);
  and and_201 (and_220_out[2], A[2], B[11]);
  and and_202 (and_220_out[1], A[1], B[11]);
  and and_203 (and_221_out[2], A[2], B[12]);
  and and_204 (and_221_out[1], A[1], B[12]);
  and and_205 (and_222_out[2], A[2], B[13]);
  and and_206 (and_222_out[1], A[1], B[13]);
  and and_207 (and_223_out[2], A[2], B[14]);
  and and_208 (and_223_out[1], A[1], B[14]);
  and and_209 (and_224_out[2], A[2], B[15]);
  and and_210 (and_224_out[1], A[1], B[15]);
  and and_211 (and_211_out[0], A[0], B[2]);
  and and_212 (and_212_out[0], A[0], B[3]);
  and and_213 (and_213_out[0], A[0], B[4]);
  and and_214 (and_214_out[0], A[0], B[5]);
  and and_215 (and_215_out[0], A[0], B[6]);
  and and_216 (and_216_out[0], A[0], B[7]);
  and and_217 (and_217_out[0], A[0], B[8]);
  and and_218 (and_218_out[0], A[0], B[9]);
  and and_219 (and_219_out[0], A[0], B[10]);
  and and_220 (and_220_out[0], A[0], B[11]);
  and and_221 (and_221_out[0], A[0], B[12]);
  and and_222 (and_222_out[0], A[0], B[13]);
  and and_223 (and_223_out[0], A[0], B[14]);
  and and_224 (and_224_out[0], A[0], B[15]);
  and and_225 (and_240_out[15], A[15], B[1]);
  and and_226 (and_240_out[14], A[14], B[1]);
  and and_227 (and_240_out[13], A[13], B[1]);
  and and_228 (and_240_out[12], A[12], B[1]);
  and and_229 (and_240_out[11], A[11], B[1]);
  and and_230 (and_240_out[10], A[10], B[1]);
  and and_231 (and_240_out[9], A[9], B[1]);
  and and_232 (and_240_out[8], A[8], B[1]);
  and and_233 (and_240_out[7], A[7], B[1]);
  and and_234 (and_240_out[6], A[6], B[1]);
  and and_235 (and_240_out[5], A[5], B[1]);
  and and_236 (and_240_out[4], A[4], B[1]);
  and and_237 (and_240_out[3], A[3], B[1]);
  and and_238 (and_240_out[2], A[2], B[1]);
  and and_239 (and_240_out[1], A[1], B[1]);
  and and_240 (and_240_out[0], A[0], B[1]);
  and and_241 (and_255_out[14], A[15], B[0]);
  and and_242 (and_255_out[13], A[14], B[0]);
  sixteen_bit_adder sixteen_bit_adder_1 (
    .A(and_240_out), .B({1'b0, and_255_out}), .Cin(1'b0), .Cout(sixteen_bit_adder_1_s[15]),
    .S({sixteen_bit_adder_1_s[14:0], Product[1]}));
  sixteen_bit_adder sixteen_bit_adder_2 (
    .A(sixteen_bit_adder_1_s), .B(and_211_out), .Cin(1'b0), .Cout(sixteen_bit_adder_2_s[15]),
    .S({sixteen_bit_adder_2_s[14:0], Product[2]}));
  sixteen_bit_adder sixteen_bit_adder_3 (
    .A(sixteen_bit_adder_2_s), .B(and_212_out), .Cin(1'b0), .Cout(sixteen_bit_adder_3_s[15]),
    .S({sixteen_bit_adder_3_s[14:0], Product[3]}));
  sixteen_bit_adder sixteen_bit_adder_4 (
    .A(sixteen_bit_adder_3_s), .B(and_213_out), .Cin(1'b0), .Cout(sixteen_bit_adder_4_s[15]),
    .S({sixteen_bit_adder_4_s[14:0], Product[4]}));
  sixteen_bit_adder sixteen_bit_adder_5 (
    .A(sixteen_bit_adder_4_s), .B(and_214_out), .Cin(1'b0), .Cout(sixteen_bit_adder_5_s[15]),
    .S({sixteen_bit_adder_5_s[14:0], Product[5]}));
  sixteen_bit_adder sixteen_bit_adder_6 (
    .A(sixteen_bit_adder_5_s), .B(and_215_out), .Cin(1'b0), .Cout(sixteen_bit_adder_6_s[15]),
    .S({sixteen_bit_adder_6_s[14:0], Product[6]}));
  sixteen_bit_adder sixteen_bit_adder_7 (
    .A(sixteen_bit_adder_6_s), .B(and_216_out), .Cin(1'b0), .Cout(sixteen_bit_adder_7_s[15]),
    .S({sixteen_bit_adder_7_s[14:0], Product[7]}));
  sixteen_bit_adder sixteen_bit_adder_8 (
    .A(sixteen_bit_adder_7_s), .B(and_217_out), .Cin(1'b0), .Cout(sixteen_bit_adder_8_s[15]),
    .S({sixteen_bit_adder_8_s[14:0], Product[8]}));
  sixteen_bit_adder sixteen_bit_adder_9 (
    .A(sixteen_bit_adder_8_s), .B(and_218_out), .Cin(1'b0), .Cout(sixteen_bit_adder_9_s[15]),
    .S({sixteen_bit_adder_9_s[14:0], Product[9]}));
  sixteen_bit_adder sixteen_bit_adder_10 (
    .A(sixteen_bit_adder_9_s), .B(and_219_out), .Cin(1'b0), .Cout(sixteen_bit_adder_10_s[15]),
    .S({sixteen_bit_adder_10_s[14:0], Product[10]}));
  sixteen_bit_adder sixteen_bit_adder_11 (
    .A(sixteen_bit_adder_10_s), .B(and_220_out), .Cin(1'b0), .Cout(sixteen_bit_adder_11_s[15]),
    .S({sixteen_bit_adder_11_s[14:0], Product[11]}));
  sixteen_bit_adder sixteen_bit_adder_12 (
    .A(sixteen_bit_adder_11_s), .B(and_221_out), .Cin(1'b0), .Cout(sixteen_bit_adder_12_s[15]),
    .S({sixteen_bit_adder_12_s[14:0], Product[12]}));
  sixteen_bit_adder sixteen_bit_adder_13 (
    .A(sixteen_bit_adder_12_s), .B(and_222_out), .Cin(1'b0), .Cout(sixteen_bit_adder_13_s[15]),
    .S({sixteen_bit_adder_13_s[14:0], Product[13]}));
  sixteen_bit_adder sixteen_bit_adder_14 (
    .A(sixteen_bit_adder_13_s), .B(and_223_out), .Cin(1'b0), .Cout(sixteen_bit_adder_14_s[15]),
    .S({sixteen_bit_adder_14_s[14:0], Product[14]}));
  sixteen_bit_adder sixteen_bit_adder_15 (
    .A(sixteen_bit_adder_14_s), .B(and_224_out), .Cin(1'b0), .Cout(Product[31]), .S(Product[30:15]));
  and and_243 (and_255_out[12], A[13], B[0]);
  and and_244 (and_255_out[11], A[12], B[0]);
  and and_245 (and_255_out[10], A[11], B[0]);
  and and_246 (and_255_out[9], A[10], B[0]);
  and and_247 (and_255_out[8], A[9], B[0]);
  and and_248 (and_255_out[7], A[8], B[0]);
  and and_249 (and_255_out[6], A[7], B[0]);
  and and_250 (and_255_out[5], A[6], B[0]);
  and and_251 (and_255_out[4], A[5], B[0]);
  and and_252 (and_255_out[3], A[4], B[0]);
  and and_253 (and_255_out[2], A[3], B[0]);
  and and_254 (and_255_out[1], A[2], B[0]);
  and and_255 (and_255_out[0], A[1], B[0]);
  and and_256 (Product[0], A[0], B[0]);
endmodule

module sixteen_bit_divider (
  input  [15:0] A,
  input  [15:0] B,
  output [15:0] Quotient,
  output [15:0] Remainder
);

  wire [15:1] sixteen_bit_adder_and_subber_1_sum, sixteen_bit_adder_and_subber_2_sum,
       sixteen_bit_adder_and_subber_3_sum, sixteen_bit_adder_and_subber_4_sum,
       sixteen_bit_adder_and_subber_5_sum, sixteen_bit_adder_and_subber_6_sum,
       sixteen_bit_adder_and_subber_7_sum, sixteen_bit_adder_and_subber_8_sum,
       sixteen_bit_adder_and_subber_9_sum, sixteen_bit_adder_and_subber_10_sum,
       sixteen_bit_adder_and_subber_11_sum, sixteen_bit_adder_and_subber_12_sum,
       sixteen_bit_adder_and_subber_13_sum, sixteen_bit_adder_and_subber_14_sum,
       sixteen_bit_adder_and_subber_15_sum;
  wire [15:15] sixteen_bit_adder_and_subber_1_sum_2, sixteen_bit_adder_and_subber_2_sum_2,
       sixteen_bit_adder_and_subber_3_sum_2, sixteen_bit_adder_and_subber_4_sum_2,
       sixteen_bit_adder_and_subber_5_sum_2, sixteen_bit_adder_and_subber_6_sum_2,
       sixteen_bit_adder_and_subber_7_sum_2, sixteen_bit_adder_and_subber_8_sum_2,
       sixteen_bit_adder_and_subber_9_sum_2, sixteen_bit_adder_and_subber_10_sum_2,
       sixteen_bit_adder_and_subber_11_sum_2, sixteen_bit_adder_and_subber_12_sum_2,
       sixteen_bit_adder_and_subber_13_sum_2, sixteen_bit_adder_and_subber_14_sum_2,
       sixteen_bit_adder_and_subber_15_sum_2;

  sixteen_bit_adder_and_subber sixteen_bit_adder_and_subber_1 (
    .A({{15{1'b0}}, A[15]}), .B(B), .Op(1'b1),
    .Sum({sixteen_bit_adder_and_subber_1_sum_2[15], sixteen_bit_adder_and_subber_1_sum}));  // open: Cout
  sixteen_bit_adder_and_subber sixteen_bit_adder_and_subber_2 (
    .A({sixteen_bit_adder_and_subber_1_sum, A[14]}), .B(B), .Op(Quotient[15]),
    .Sum({sixteen_bit_adder_and_subber_2_sum_2[15], sixteen_bit_adder_and_subber_2_sum}));  // open: Cout
  sixteen_bit_adder_and_subber sixteen_bit_adder_and_subber_3 (
    .A({sixteen_bit_adder_and_subber_2_sum, A[13]}), .B(B), .Op(Quotient[14]),
    .Sum({sixteen_bit_adder_and_subber_3_sum_2[15], sixteen_bit_adder_and_subber_3_sum}));  // open: Cout
  sixteen_bit_adder_and_subber sixteen_bit_adder_and_subber_4 (
    .A({sixteen_bit_adder_and_subber_3_sum, A[12]}), .B(B), .Op(Quotient[13]),
    .Sum({sixteen_bit_adder_and_subber_4_sum_2[15], sixteen_bit_adder_and_subber_4_sum}));  // open: Cout
  sixteen_bit_adder_and_subber sixteen_bit_adder_and_subber_5 (
    .A({sixteen_bit_adder_and_subber_4_sum, A[11]}), .B(B), .Op(Quotient[12]),
    .Sum({sixteen_bit_adder_and_subber_5_sum_2[15], sixteen_bit_adder_and_subber_5_sum}));  // open: Cout
  sixteen_bit_adder_and_subber sixteen_bit_adder_and_subber_6 (
    .A({sixteen_bit_adder_and_subber_5_sum, A[10]}), .B(B), .Op(Quotient[11]),
    .Sum({sixteen_bit_adder_and_subber_6_sum_2[15], sixteen_bit_adder_and_subber_6_sum}));  // open: Cout
  sixteen_bit_adder_and_subber sixteen_bit_adder_and_subber_7 (
    .A({sixteen_bit_adder_and_subber_6_sum, A[9]}), .B(B), .Op(Quotient[10]),
    .Sum({sixteen_bit_adder_and_subber_7_sum_2[15], sixteen_bit_adder_and_subber_7_sum}));  // open: Cout
  sixteen_bit_adder_and_subber sixteen_bit_adder_and_subber_8 (
    .A({sixteen_bit_adder_and_subber_7_sum, A[8]}), .B(B), .Op(Quotient[9]),
    .Sum({sixteen_bit_adder_and_subber_8_sum_2[15], sixteen_bit_adder_and_subber_8_sum}));  // open: Cout
  sixteen_bit_adder_and_subber sixteen_bit_adder_and_subber_9 (
    .A({sixteen_bit_adder_and_subber_8_sum, A[7]}), .B(B), .Op(Quotient[8]),
    .Sum({sixteen_bit_adder_and_subber_9_sum_2[15], sixteen_bit_adder_and_subber_9_sum}));  // open: Cout
  sixteen_bit_adder_and_subber sixteen_bit_adder_and_subber_10 (
    .A({sixteen_bit_adder_and_subber_9_sum, A[6]}), .B(B), .Op(Quotient[7]),
    .Sum({sixteen_bit_adder_and_subber_10_sum_2[15], sixteen_bit_adder_and_subber_10_sum}));  // open: Cout
  sixteen_bit_adder_and_subber sixteen_bit_adder_and_subber_11 (
    .A({sixteen_bit_adder_and_subber_10_sum, A[5]}), .B(B), .Op(Quotient[6]),
    .Sum({sixteen_bit_adder_and_subber_11_sum_2[15], sixteen_bit_adder_and_subber_11_sum}));  // open: Cout
  sixteen_bit_adder_and_subber sixteen_bit_adder_and_subber_12 (
    .A({sixteen_bit_adder_and_subber_11_sum, A[4]}), .B(B), .Op(Quotient[5]),
    .Sum({sixteen_bit_adder_and_subber_12_sum_2[15], sixteen_bit_adder_and_subber_12_sum}));  // open: Cout
  sixteen_bit_adder_and_subber sixteen_bit_adder_and_subber_13 (
    .A({sixteen_bit_adder_and_subber_12_sum, A[3]}), .B(B), .Op(Quotient[4]),
    .Sum({sixteen_bit_adder_and_subber_13_sum_2[15], sixteen_bit_adder_and_subber_13_sum}));  // open: Cout
  sixteen_bit_adder_and_subber sixteen_bit_adder_and_subber_14 (
    .A({sixteen_bit_adder_and_subber_13_sum, A[2]}), .B(B), .Op(Quotient[3]),
    .Sum({sixteen_bit_adder_and_subber_14_sum_2[15], sixteen_bit_adder_and_subber_14_sum}));  // open: Cout
  sixteen_bit_adder_and_subber sixteen_bit_adder_and_subber_15 (
    .A({sixteen_bit_adder_and_subber_14_sum, A[1]}), .B(B), .Op(Quotient[2]),
    .Sum({sixteen_bit_adder_and_subber_15_sum_2[15], sixteen_bit_adder_and_subber_15_sum}));  // open: Cout
  sixteen_bit_adder_and_subber sixteen_bit_adder_and_subber_16 (
    .A({sixteen_bit_adder_and_subber_15_sum, A[0]}), .B(B), .Op(Quotient[1]), .Sum(Remainder));  // open: Cout
  not not_1 (Quotient[15], sixteen_bit_adder_and_subber_1_sum_2[15]);
  not not_2 (Quotient[14], sixteen_bit_adder_and_subber_2_sum_2[15]);
  not not_3 (Quotient[13], sixteen_bit_adder_and_subber_3_sum_2[15]);
  not not_4 (Quotient[12], sixteen_bit_adder_and_subber_4_sum_2[15]);
  not not_5 (Quotient[11], sixteen_bit_adder_and_subber_5_sum_2[15]);
  not not_6 (Quotient[10], sixteen_bit_adder_and_subber_6_sum_2[15]);
  not not_7 (Quotient[9], sixteen_bit_adder_and_subber_7_sum_2[15]);
  not not_8 (Quotient[8], sixteen_bit_adder_and_subber_8_sum_2[15]);
  not not_9 (Quotient[7], sixteen_bit_adder_and_subber_9_sum_2[15]);
  not not_10 (Quotient[6], sixteen_bit_adder_and_subber_10_sum_2[15]);
  not not_11 (Quotient[5], sixteen_bit_adder_and_subber_11_sum_2[15]);
  not not_12 (Quotient[4], sixteen_bit_adder_and_subber_12_sum_2[15]);
  not not_13 (Quotient[3], sixteen_bit_adder_and_subber_13_sum_2[15]);
  not not_14 (Quotient[2], sixteen_bit_adder_and_subber_14_sum_2[15]);
  not not_15 (Quotient[1], sixteen_bit_adder_and_subber_15_sum_2[15]);
  not not_16 (Quotient[0], Remainder[15]);
endmodule

module sixteen_bit_comparator (
  input  [3:0] A,
  input  [3:0] B,
  output greater_than,
  output equal_to,
  output less_than
);
endmodule

module alu (
  input  [15:0] A,
  input  [15:0] B,
  input  [4:0] Op
);

  sixteen_bit_adder_and_subber sixteen_bit_adder_and_subber_1 (.A(A), .B(B), .Op(1'b0));  // open: Cout, Sum
  sixteen_bit_adder_and_subber sixteen_bit_adder_and_subber_2 (.A(A), .B(B), .Op(1'b1));  // open: Cout, Sum
  sixteen_bit_multiplier sixteen_bit_multiplier_1 (.A(A), .B(B));  // open: Product
  // NOT_Gate not_1 is placed but not wired
  // AND_Gate and_1 is placed but not wired
  // OR_Gate or_1 is placed but not wired
  // NAND_Gate nand_1 is placed but not wired
  // NOR_Gate nor_1 is placed but not wired
  // XOR_Gate xor_1 is placed but not wired
  // XNOR_Gate xnor_1 is placed but not wired
  Multiplexer #(.enable("false")) multiplexer_1 ();  // open: in0, in1, out, sel

  // Notes on the sheet:
  //   0 ADD, 1 SUB, 2 MUL, 3 DIV, 4 SHR, 5 SHL, 6 INC, 7 DEC, 8 CMP, 9 NOT, 10 AND, 11 OR, 12 NAND, 13 NOR,  14 XOR, 15 XNOR
endmodule

module main (
  input  [15:0] in_1,
  input  [15:0] in_2,
  output [15:0] out_3,
  output [15:0] out_4
);

  sixteen_bit_divider sixteen_bit_divider_1 (.A(in_1), .B(in_2), .Quotient(out_3), .Remainder(out_4));
endmodule
